# Fritzing sketch TLC5940 (saved by Fritzing 0.8.0b)
breadboards: 1

parts:
  Raspberry_Pi1 = Raspberry Pi (Model B)
  TLC5940NT1 = TLC5940NT [package="DIP (Dual Inline)"]
  R2 = Resistor [tolerance=±1% resistance=2k package="1206 [SMD]"]

nets:
  5V: Raspberry_Pi1.5V, TLC5940NT1.DCPRG, TLC5940NT1.VCC
  GND: Raspberry_Pi1.GND, TLC5940NT1.GND, R2.Pin_0
  N1: Raspberry_Pi1.#22, TLC5940NT1.BLANK
  N2: Raspberry_Pi1.#23, TLC5940NT1.GSCLK
  N3: Raspberry_Pi1.#24, TLC5940NT1.VPRG
  N4: Raspberry_Pi1.MOSI, TLC5940NT1.SIN
  N5: Raspberry_Pi1.SCLK, TLC5940NT1.SCLK
  N6: Raspberry_Pi1.CS0, TLC5940NT1.XLAT
  N7: TLC5940NT1.IREF, R2.Pin_1

custom parts:
  Raspberry Pi (Model B): Raspberry Pi Single-board Computer, Model B
  TLC5940NT: The TLC5940 is a 16-channel, constant-current sink, LED driver. Each channel has an individually adjustable 4096-step grayscale PWM brightness control and a 64-step constant-current sink (dot correction).
